// Logisim project DPCOTEAM.circ as structural Verilog: 1 circuit, main circuit main
module main (
  input  _0,
  input  _1,
  input  _2,
  input  _3,
  input  _4,
  input  _5,
  input  _6,
  input  _7,
  input  _8,
  input  _9,
  input  A,
  input  B,
  input  C,
  input  D,
  input  E,
  input  F,
  output out_17,
  output out_18,
  output out_19,
  output out_20
);

  or or_1 (out_17, _8, _9, A, B, C, D, E, F);
  or or_2 (out_18, _4, _5, _5, _6, C, D, E, F);
  or or_3 (out_19, _2, _3, _6, _7, A, B, E, F);
  or or_4 (out_20, _1, _3, _5, _7, _9, B, D, F);
endmodule
